# Fritzing sketch 6x6_rgb_led_matrix (saved by Fritzing 0.9.3b)
circuit board: 17.9109cm x 20.8498cm
breadboards: 3

parts:
  GND_CTRL = SHIFT REGISTER [package=dil16]
  GREEN_CTRL = SHIFT REGISTER [package=dil16]
  BLUE_CTRL = SHIFT REGISTER [package=dil16]
  RED_CTRL = SHIFT REGISTER [package=dil16]
  Part1 = Arduino Uno (Rev3) - ICSP
  G_1 = Resistor [tolerance=±5% resistance=100 package=THT]
  R_3 = Resistor [tolerance=±5% resistance=150 package=THT]
  B_2 = Resistor [tolerance=±5% resistance=220 package=THT]
  G_5 = Resistor [tolerance=±5% resistance=100 package=THT]
  B_5 = Resistor [tolerance=±5% resistance=220 package=THT]
  G_2 = Resistor [tolerance=±5% resistance=100 package=THT]
  R_2 = Resistor [tolerance=±5% resistance=150 package=THT]
  B_1 = Resistor [tolerance=±5% resistance=220 package=THT]
  B_3 = Resistor [tolerance=±5% resistance=220 package=THT]
  R_4 = Resistor [tolerance=±5% resistance=150 package=THT]
  G_4 = Resistor [tolerance=±5% resistance=100 package=THT]
  B_4 = Resistor [tolerance=±5% resistance=220 package=THT]
  R_5 = Resistor [tolerance=±5% resistance=150 package=THT]
  G_0 = Resistor [tolerance=±5% resistance=100 package=THT]
  G_3 = Resistor [tolerance=±5% resistance=100 package=THT]
  R_0 = Resistor [tolerance=±5% resistance=150 package=THT]
  R_1 = Resistor [tolerance=±5% resistance=150 package=THT]
  B_0 = Resistor [tolerance=±5% resistance=220 package=THT]
  RGB_1_0 = RGB LED (com. cathode, rgb) [package="5 mm [THT]"]
  RGB_3_0 = RGB LED (com. cathode, rgb) [package="5 mm [THT]"]
  RGB_5_0 = RGB LED (com. cathode, rgb) [package="5 mm [THT]"]
  RGB_0_1 = RGB LED (com. cathode, rgb) [package="5 mm [THT]"]
  RGB_1_1 = RGB LED (com. cathode, rgb) [package="5 mm [THT]"]
  RGB_2_1 = RGB LED (com. cathode, rgb) [package="5 mm [THT]"]
  RGB_3_1 = RGB LED (com. cathode, rgb) [package="5 mm [THT]"]
  RGB_4_1 = RGB LED (com. cathode, rgb) [package="5 mm [THT]"]
  RGB_5_1 = RGB LED (com. cathode, rgb) [package="5 mm [THT]"]
  RGB_0_2 = RGB LED (com. cathode, rgb) [package="5 mm [THT]"]
  RGB_1_2 = RGB LED (com. cathode, rgb) [package="5 mm [THT]"]
  RGB_2_2 = RGB LED (com. cathode, rgb) [package="5 mm [THT]"]
  RGB_3_2 = RGB LED (com. cathode, rgb) [package="5 mm [THT]"]
  RGB_4_2 = RGB LED (com. cathode, rgb) [package="5 mm [THT]"]
  RGB_5_2 = RGB LED (com. cathode, rgb) [package="5 mm [THT]"]
  RGB_1_3 = RGB LED (com. cathode, rgb) [package="5 mm [THT]"]
  RGB_2_3 = RGB LED (com. cathode, rgb) [package="5 mm [THT]"]
  RGB_3_3 = RGB LED (com. cathode, rgb) [package="5 mm [THT]"]
  RGB_4_3 = RGB LED (com. cathode, rgb) [package="5 mm [THT]"]
  RGB_5_3 = RGB LED (com. cathode, rgb) [package="5 mm [THT]"]
  RGB_0_4 = RGB LED (com. cathode, rgb) [package="5 mm [THT]"]
  RGB_1_4 = RGB LED (com. cathode, rgb) [package="5 mm [THT]"]
  RGB_2_4 = RGB LED (com. cathode, rgb) [package="5 mm [THT]"]
  RGB_3_4 = RGB LED (com. cathode, rgb) [package="5 mm [THT]"]
  RGB_4_4 = RGB LED (com. cathode, rgb) [package="5 mm [THT]"]
  RGB_5_4 = RGB LED (com. cathode, rgb) [package="5 mm [THT]"]
  RGB_0_5 = RGB LED (com. cathode, rgb) [package="5 mm [THT]"]
  RGB_1_5 = RGB LED (com. cathode, rgb) [package="5 mm [THT]"]
  RGB_2_5 = RGB LED (com. cathode, rgb) [package="5 mm [THT]"]
  RGB_3_5 = RGB LED (com. cathode, rgb) [package="5 mm [THT]"]
  RGB_4_5 = RGB LED (com. cathode, rgb) [package="5 mm [THT]"]
  RGB_5_5 = RGB LED (com. cathode, rgb) [package="5 mm [THT]"]
  RGB_4_0 = RGB LED (com. cathode, rgb) [package="5 mm [THT]"]
  J1 = Camdenboss CTB0158-12 [part_number=CTB0158-12 package=THT]
  RGB_0_0 = RGB LED (com. cathode, rgb) [package="5 mm [THT]"]
  RGB_2_0 = RGB LED (com. cathode, rgb) [package="5 mm [THT]"]
  J2 = Screw terminal - 2 pins [package=THT]
  RGB_0_3 = RGB LED (com. cathode, rgb) [package="5 mm [THT]"]

nets:
  N1: GND_CTRL.QB, RGB_1_0.common_cathode, RGB_3_0.common_cathode, RGB_5_0.common_cathode, RGB_4_0.common_cathode, RGB_0_0.common_cathode, RGB_2_0.common_cathode
  N2: GND_CTRL.QC, RGB_0_1.common_cathode, RGB_1_1.common_cathode, RGB_2_1.common_cathode, RGB_3_1.common_cathode, RGB_4_1.common_cathode, RGB_5_1.common_cathode
  N3: GND_CTRL.QD, RGB_0_2.common_cathode, RGB_1_2.common_cathode, RGB_2_2.common_cathode, RGB_3_2.common_cathode, RGB_4_2.common_cathode, RGB_5_2.common_cathode
  N4: GND_CTRL.QE, RGB_1_3.common_cathode, RGB_2_3.common_cathode, RGB_3_3.common_cathode, RGB_4_3.common_cathode, RGB_5_3.common_cathode, RGB_0_3.common_cathode
  N5: GND_CTRL.QF, RGB_0_4.common_cathode, RGB_1_4.common_cathode, RGB_2_4.common_cathode, RGB_3_4.common_cathode, RGB_4_4.common_cathode, RGB_5_4.common_cathode
  N6: GND_CTRL.QG, RGB_0_5.common_cathode, RGB_1_5.common_cathode, RGB_2_5.common_cathode, RGB_3_5.common_cathode, RGB_4_5.common_cathode, RGB_5_5.common_cathode
  GND: GND_CTRL.GND, GREEN_CTRL.GND, RED_CTRL.G
  N7: GND_CTRL.RCK, Part1.D2, J1.pin10
  GND_2: GND_CTRL.G, GREEN_CTRL.G, BLUE_CTRL.GND, Part1.GND
  N8: GND_CTRL.SER, Part1.D3_PWM, J1.pin11
  N9: GND_CTRL.QA, Part1.D4, J1.pin12
  VCC: GND_CTRL.VCC, GREEN_CTRL.VCC, BLUE_CTRL.VCC, RED_CTRL.VCC, Part1.5V, J2.pin2
  N10: GREEN_CTRL.QB, G_0.Pin_1
  N11: GREEN_CTRL.QC, G_1.Pin_1
  N12: GREEN_CTRL.QD, G_2.Pin_1
  N13: GREEN_CTRL.QE, G_3.Pin_1
  N14: GREEN_CTRL.QF, G_4.Pin_1
  N15: GREEN_CTRL.QG, G_5.Pin_1
  N16: GREEN_CTRL.RCK, Part1.D8, J1.pin4
  N17: GREEN_CTRL.SER, Part1.D9_PWM, J1.pin5
  N18: GREEN_CTRL.QA, Part1.D10_PWM/SS, J1.pin6
  N19: BLUE_CTRL.QB, B_0.Pin_1
  N20: BLUE_CTRL.QC, B_1.Pin_1
  N21: BLUE_CTRL.QD, B_2.Pin_1
  N22: BLUE_CTRL.QE, B_3.Pin_1
  N23: BLUE_CTRL.QF, B_4.Pin_1
  N24: BLUE_CTRL.QG, B_5.Pin_1
  N25: BLUE_CTRL.RCK, Part1.D11_PWM/MOSI, J1.pin1
  N26: BLUE_CTRL.G, J2.pin1
  N27: BLUE_CTRL.SER, Part1.D12/MISO, J1.pin2
  N28: BLUE_CTRL.QA, Part1.D13/SCK, J1.pin3
  N29: RED_CTRL.QB, R_0.Pin_1
  N30: RED_CTRL.QC, R_1.Pin_1
  N31: RED_CTRL.QD, R_2.Pin_1
  N32: RED_CTRL.QE, R_3.Pin_1
  N33: RED_CTRL.QF, R_4.Pin_1
  N34: RED_CTRL.QG, R_5.Pin_1
  N35: RED_CTRL.RCK, Part1.D5_PWM, J1.pin7
  N36: RED_CTRL.SER, Part1.D6_PWM, J1.pin8
  N37: RED_CTRL.QA, Part1.D7, J1.pin9
  N38: G_1.Pin_0, RGB_1_0.green_anode, RGB_1_1.green_anode, RGB_1_2.green_anode, RGB_1_3.green_anode, RGB_1_4.green_anode, RGB_1_5.green_anode
  N39: R_3.Pin_0, RGB_3_0.red_anode, RGB_3_1.red_anode, RGB_3_2.red_anode, RGB_3_3.red_anode, RGB_3_4.red_anode, RGB_3_5.red_anode
  N40: B_2.Pin_0, RGB_2_1.blue_anode, RGB_2_2.blue_anode, RGB_2_3.blue_anode, RGB_2_4.blue_anode, RGB_2_5.blue_anode, RGB_2_0.blue_anode
  N41: G_5.Pin_0, RGB_5_0.green_anode, RGB_5_1.green_anode, RGB_5_2.green_anode, RGB_5_3.green_anode, RGB_5_4.green_anode, RGB_5_5.green_anode
  N42: B_5.Pin_0, RGB_5_0.blue_anode, RGB_5_1.blue_anode, RGB_5_2.blue_anode, RGB_5_3.blue_anode, RGB_5_4.blue_anode, RGB_5_5.blue_anode
  N43: G_2.Pin_0, RGB_2_1.green_anode, RGB_2_2.green_anode, RGB_2_3.green_anode, RGB_2_4.green_anode, RGB_2_5.green_anode, RGB_2_0.green_anode
  N44: R_2.Pin_0, RGB_2_1.red_anode, RGB_2_2.red_anode, RGB_2_3.red_anode, RGB_2_4.red_anode, RGB_2_5.red_anode, RGB_2_0.red_anode
  N45: B_1.Pin_0, RGB_1_0.blue_anode, RGB_1_1.blue_anode, RGB_1_2.blue_anode, RGB_1_3.blue_anode, RGB_1_4.blue_anode, RGB_1_5.blue_anode
  N46: B_3.Pin_0, RGB_3_0.blue_anode, RGB_3_1.blue_anode, RGB_3_2.blue_anode, RGB_3_3.blue_anode, RGB_3_4.blue_anode, RGB_3_5.blue_anode
  N47: R_4.Pin_0, RGB_4_1.red_anode, RGB_4_2.red_anode, RGB_4_3.red_anode, RGB_4_4.red_anode, RGB_4_5.red_anode, RGB_4_0.red_anode
  N48: G_4.Pin_0, RGB_4_1.green_anode, RGB_4_2.green_anode, RGB_4_3.green_anode, RGB_4_4.green_anode, RGB_4_5.green_anode, RGB_4_0.green_anode
  N49: B_4.Pin_0, RGB_4_1.blue_anode, RGB_4_2.blue_anode, RGB_4_3.blue_anode, RGB_4_4.blue_anode, RGB_4_5.blue_anode, RGB_4_0.blue_anode
  N50: R_5.Pin_0, RGB_5_0.red_anode, RGB_5_1.red_anode, RGB_5_2.red_anode, RGB_5_3.red_anode, RGB_5_4.red_anode, RGB_5_5.red_anode
  N51: G_0.Pin_0, RGB_0_1.green_anode, RGB_0_2.green_anode, RGB_0_4.green_anode, RGB_0_5.green_anode, RGB_0_0.green_anode, RGB_0_3.green_anode
  N52: G_3.Pin_0, RGB_3_0.green_anode, RGB_3_1.green_anode, RGB_3_2.green_anode, RGB_3_3.green_anode, RGB_3_4.green_anode, RGB_3_5.green_anode
  N53: R_0.Pin_0, RGB_0_1.red_anode, RGB_0_2.red_anode, RGB_0_4.red_anode, RGB_0_5.red_anode, RGB_0_0.red_anode, RGB_0_3.red_anode
  N54: R_1.Pin_0, RGB_1_0.red_anode, RGB_1_1.red_anode, RGB_1_2.red_anode, RGB_1_3.red_anode, RGB_1_4.red_anode, RGB_1_5.red_anode
  N55: B_0.Pin_0, RGB_0_1.blue_anode, RGB_0_2.blue_anode, RGB_0_4.blue_anode, RGB_0_5.blue_anode, RGB_0_0.blue_anode, RGB_0_3.blue_anode
